// Logisim project TTL-Computer.circ as structural Verilog
module Program_Counter (
);

  // _74191 74191_1: pin names not known
  // _74191 74191_2: pin names not known
  // _74191 74191_3: pin names not known
  // _74191 74191_4: pin names not known
endmodule

module Sequencer_Instruction_Decoder (
  input  nOE,
  input  RESTART,
  input  LOAD
);

  wire and_1_out, and_3_out, and_4_out, and_5_out, CLOCK_out, dip_7474_1_p1, dip_7474_1_p2, dip_7474_1_p4,
       dip_74161_1_p1, dip_74161_1_p3, dip_74161_1_p5, dip_74161_1_p7, dip_74161_1_p9, dip_74161_1_p13,
       dip_74161_2_p2, dip_74161_2_p9, dip_74161_2_p13, dip_74595_1_p1, dip_74595_1_p2, dip_74595_1_p3,
       dip_74595_1_p5, dip_74595_1_p6, dip_74595_1_p7, dip_74595_1_p9, dip_74595_1_p10, dip_74595_1_p11,
       dip_74595_1_p12, dip_74595_1_p13, dip_74595_1_p15, dip_74595_1_p17, dip_74595_2_p1, dip_74595_2_p3,
       dip_74595_2_p5, dip_74595_2_p6, dip_74595_2_p7, dip_74595_2_p8, dip_74595_2_p9, dip_74595_2_p11,
       dip_74595_2_p13, dip_74595_3_p1, dip_74595_3_p3, dip_74595_3_p5, dip_74595_3_p6, dip_74595_3_p7,
       dip_74595_3_p8, dip_74595_3_p9, dip_74595_3_p11, dip_74595_3_p13, dip_74595_4_p1, dip_74595_4_p3,
       dip_74595_4_p5, dip_74595_4_p6, dip_74595_4_p7, dip_74595_4_p8, dip_74595_4_p9, dip_74595_4_p11,
       dip_74595_4_p13, dip_74595_5_p1, dip_74595_5_p3, dip_74595_5_p5, dip_74595_5_p6, dip_74595_5_p7,
       dip_74595_5_p8, dip_74595_5_p9, dip_74595_5_p11, dip_74595_5_p13, dip_74595_6_p1, dip_74595_6_p3,
       dip_74595_6_p5, dip_74595_6_p7, dip_74595_6_p8, dip_74595_6_p9, n74165_1_p1, n74165_1_p2,
       n74165_1_p13, not_1_out, not_3_out, not_4_out, not_6_out, not_7_out, not_8_out, or_1_out, or_2_out;
  wire [2:0] dip_74161_2_p3;
  wire [7:0] rom_1_data;

  ROM #(.addrWidth(19)) rom_1 (.addr({{16{1'b0}}, dip_74161_2_p3}), .data(rom_1_data), .sel(1'b1));
  // _74165 74165_1: pin names not known; wires that end beside it: n74165_1_p1, n74165_1_p2, rom_1_data[4], rom_1_data[5], rom_1_data[6], rom_1_data[7], 1'b0, rom_1_data[3], rom_1_data[2], rom_1_data[1], rom_1_data[0], 1'b0, n74165_1_p13
  nor nor_1 (n74165_1_p1, LOAD, and_1_out);
  DotMatrix #(.matrixcols(24), .matrixrows(1), .dotshape("circle")) dotmatrix_1 (
    .col0(dip_74595_1_p1), .col1(dip_74595_1_p3), .col2(dip_74595_1_p5), .col3(dip_74595_1_p7),
    .col4(dip_74595_1_p9), .col5(dip_74595_1_p11), .col6(dip_74595_1_p13), .col7(dip_74595_1_p12),
    .col8(dip_74595_1_p15), .col9(dip_74595_1_p17), .col10(dip_74595_2_p1), .col11(dip_74595_2_p3),
    .col12(dip_74595_2_p5), .col13(dip_74595_2_p7), .col14(dip_74595_2_p9), .col15(dip_74595_2_p8),
    .col16(dip_74595_2_p11), .col17(dip_74595_2_p13), .col18(dip_74595_3_p1), .col19(dip_74595_3_p3),
    .col20(dip_74595_3_p5), .col21(dip_74595_3_p7), .col22(dip_74595_3_p9), .col23(dip_74595_3_p8));
  // DIP_74595 dip_74595_1: pin names not known; wires that end beside it: dip_74595_1_p1, dip_74595_1_p2, dip_74595_1_p3, n74165_1_p2, dip_74595_1_p5, dip_74595_1_p6, dip_74595_1_p7, nOE, dip_74595_1_p9, dip_74595_1_p10, dip_74595_1_p11, dip_74595_1_p12, dip_74595_1_p13, dip_74595_1_p10, dip_74595_1_p15, dip_74595_1_p2, dip_74595_1_p17, n74165_1_p2
  // DIP_74595 dip_74595_2: pin names not known; wires that end beside it: dip_74595_2_p1, dip_74595_1_p6, dip_74595_2_p3, nOE, dip_74595_2_p5, dip_74595_2_p6, dip_74595_2_p7, dip_74595_2_p8, dip_74595_2_p9, dip_74595_2_p6, dip_74595_2_p11, dip_74595_1_p2, dip_74595_2_p13, n74165_1_p2
  // DIP_74595 dip_74595_3: pin names not known; wires that end beside it: dip_74595_3_p1, dip_74595_1_p6, dip_74595_3_p3, nOE, dip_74595_3_p5, dip_74595_3_p6, dip_74595_3_p7, dip_74595_3_p8, dip_74595_3_p9, dip_74595_3_p6, dip_74595_3_p11, dip_74595_1_p2, dip_74595_3_p13, n74165_1_p2
  and and_1 (and_1_out, and_4_out, CLOCK_out);
  DotMatrix #(.matrixcols(24), .matrixrows(1), .dotshape("circle")) dotmatrix_2 (
    .col0(dip_74595_3_p11), .col1(dip_74595_3_p13), .col2(dip_74595_4_p1), .col3(dip_74595_4_p3),
    .col4(dip_74595_4_p5), .col5(dip_74595_4_p7), .col6(dip_74595_4_p9), .col7(dip_74595_4_p8),
    .col8(dip_74595_4_p11), .col9(dip_74595_4_p13), .col10(dip_74595_5_p1), .col11(dip_74595_5_p3),
    .col12(dip_74595_5_p5), .col13(dip_74595_5_p7), .col14(dip_74595_5_p9), .col15(dip_74595_5_p8),
    .col16(dip_74595_5_p11), .col17(dip_74595_5_p13), .col18(dip_74595_6_p1), .col19(dip_74595_6_p3),
    .col20(dip_74595_6_p5), .col21(dip_74595_6_p7), .col22(dip_74595_6_p9), .col23(dip_74595_6_p8));
  nor nor_2 (dip_74595_1_p2, n74165_1_p1, or_1_out);
  // DIP_74595 dip_74595_4: pin names not known; wires that end beside it: dip_74595_4_p1, dip_74595_1_p6, dip_74595_4_p3, nOE, dip_74595_4_p5, dip_74595_4_p6, dip_74595_4_p7, dip_74595_4_p8, dip_74595_4_p9, dip_74595_4_p6, dip_74595_4_p11, dip_74595_1_p2, dip_74595_4_p13, n74165_1_p2
  and and_2 (n74165_1_p2, and_3_out, not_3_out);
  and and_3 (and_3_out, or_2_out, CLOCK_out);
  or or_1 (or_1_out, and_4_out, not_1_out);
  not not_1 (not_1_out, CLOCK_out);
  or or_2 (or_2_out, n74165_1_p1, and_4_out);
  Clock CLOCK (.out(CLOCK_out));
  // DIP_74595 dip_74595_5: pin names not known; wires that end beside it: dip_74595_5_p1, dip_74595_1_p6, dip_74595_5_p3, nOE, dip_74595_5_p5, dip_74595_5_p6, dip_74595_5_p7, dip_74595_5_p8, dip_74595_5_p9, dip_74595_5_p6, dip_74595_5_p11, dip_74595_1_p2, dip_74595_5_p13, n74165_1_p2
  not not_2 (dip_74595_1_p6, n74165_1_p2);
  not not_3 (not_3_out, and_5_out);
  // DIP_74595 dip_74595_6: pin names not known; wires that end beside it: dip_74595_6_p1, dip_74595_1_p6, dip_74595_6_p3, nOE, dip_74595_6_p5, n74165_1_p13, dip_74595_6_p7, dip_74595_6_p8, dip_74595_6_p9
  DotMatrix #(.matrixcols(4), .matrixrows(1), .dotshape("circle")) dotmatrix_3 (
    .col0(dip_74161_1_p9), .col1(dip_74161_1_p7), .col2(dip_74161_1_p5), .col3(dip_74161_1_p3));
  and and_4 (and_4_out, dip_74161_1_p3, dip_74161_1_p5, dip_74161_1_p7);
  // DIP_74161 dip_74161_1: pin names not known; wires that end beside it: dip_74161_1_p1, n74165_1_p2, dip_74161_1_p3, 1'b0, dip_74161_1_p5, 1'b0, dip_74161_1_p7, 1'b0, dip_74161_1_p9, 1'b0, 1'b1, 1'b1, dip_74161_1_p13
  or or_3 (dip_74161_1_p1, and_4_out, n74165_1_p1);
  and and_5 (and_5_out, dip_7474_1_p4, not_4_out);
  not not_4 (not_4_out, LOAD);
  not not_5 (dip_74161_1_p13, and_4_out);
  not not_6 (not_6_out, dip_74595_1_p2);
  // Probe on dip_74161_2_p2
  not not_7 (not_7_out, and_4_out);
  not not_8 (not_8_out, CLOCK_out);
  DotMatrix #(.matrixcols(4), .matrixrows(1), .dotshape("circle")) dotmatrix_4 (
    .col0(dip_74161_2_p9), .col1(dip_74161_2_p3[2]), .col2(dip_74161_2_p3[1]), .col3(dip_74161_2_p3[0]));
  // DIP_74161 dip_74161_2: pin names not known; wires that end beside it: not_6_out, dip_74161_2_p2, dip_74161_2_p3[0], 1'b0, dip_74161_2_p3[1], 1'b0, dip_74161_2_p3[2], 1'b0, dip_74161_2_p9, 1'b0, 1'b1, 1'b1, dip_74161_2_p13
  // AND_Gate and_6 has open pins: in1=n74165_1_p2, out=open
  nor nor_3 (dip_74161_2_p2, not_7_out, n74165_1_p2, not_8_out);
  // DIP_7474 dip_7474_1: pin names not known; wires that end beside it: dip_7474_1_p1, dip_7474_1_p2, dip_7474_1_p2, dip_7474_1_p4
  not not_9 (dip_7474_1_p1, LOAD);
  not not_10 (dip_74161_2_p13, RESTART);
  and and_7 (dip_7474_1_p2, dip_74161_2_p3[1], dip_74161_2_p3[2]);

  // Notes on the sheet:
  //   nOE: pull=down
  //   RESTART: pull=down
  //   LOAD: pull=down
  //   CONTROL ROM
  //   contents of rom_1 (hex, n*v repeats v):
  //   aa cc ff bb ee 99
  //   SH/~LR
  //   ROM DATA
  //   DATA
  //   NEXT_BIT
  //   ~CLR
  //   ~CLR
  //   SHIFT REGISTER DATA
  //   RCLK
  //   SRCLK
  //   DATA
  //   DATA BIT COUNTER
  //   CLR
  //   NEXT_BIT
  //   DONE
  //   CE
  //   CLR
  //   RESTART
  //   DATA BYTE COUNTER
  //   CE
endmodule
